# Fritzing sketch VKB_Grip_Schematic (saved by Fritzing 0.9.9b)
breadboards: 1

parts:
  Part1 = Arduino Pro Micro (Clone)
  R1 = Resistor [tolerance=±5% power=0.25 resistance=3k package=THT]
  R2 = Resistor [tolerance=±5% power=0.25 resistance=103k package=THT]
  A1 = AMS11176 module

nets:
  N1: Part1.TXO, R1.Pin_1
  N2: Part1.RXI, R1.Pin_0, R2.Pin_1
  N3: Part1.GND, R2.Pin_0, A1.pin3
  N4: Part1.VCC, A1.pin1

notes:
  GND to VKB
  3.3V to VKB
  Data Pin to VKB
  AMS1117-3.3
  3.3V VREG

custom parts:
  AMS11176 module: DC-DC step-down modules ( input DC 4.5～7V , output DC 3.3V ).
